# Fritzing sketch pcb (saved by Fritzing 1.0.4)

parts:
  Driver1 = 28BYJ-48 Driver Module [part_number=ULN2003 package=THT]
  U1 = LuaNode32 / ESP32
  R1 = Resistor [tolerance=±5% power=0.25W resistance=220 package=THT]
  R2 = Resistor [tolerance=±5% power=0.25W resistance=220 package=THT]
  TP1 = TP4056 [chip_label=TP4056 package="DIP (Dual Inline) [THT]"]
  M1 = MT3608 Module
  D2 = Diode [package=diode-1n4001]
  R3 = Resistor [tolerance=±5% resistance=220 package="0603 [SMD]"]
  U3 = TL431 (sot23) [package=sot23]
  btn = Screw terminal - 2 pins [package=THT]
  R4 = Resistor [tolerance=±5% power=0.25W resistance=100k package=THT]
  R5 = Resistor [tolerance=±5% power=0.25W resistance=100k package=THT]
  OLED1 = Header 4 [package=screwterminal-3.5mm-4_lock]
  LED1 = Header 4 [package=screwterminal-3.5mm-4_lock]
  ds1307 = Header 6 [package=molex-1x6-ra]
  bat = Screw terminal - 2 pins [package=THT]
  pwr = Screw terminal - 2 pins [package=THT]
  solar = Screw terminal - 2 pins [package=THT]
  pwrsw = Screw terminal - 2 pins [package=THT]

nets:
  N1: Driver1.IN1, U1.D26
  N2: Driver1.IN2, U1.D25
  N3: Driver1.IN3, U1.D33
  N4: Driver1.IN4, U1.D32
  GND: Driver1.GND, U1.GND, TP1.pin6, M1.pin1, M1.pin4, U3.2, btn.pin2, OLED1.3, ds1307.1
  N5: Driver1.Vmotor, U1.Vin, M1.pin3, R3.Pin_1
  N6: U1.VP, R1.Pin_0, R2.Pin_1
  N7: U1.D35, R4.Pin_1, R5.Pin_0
  N8: U1.D27, LED1.4
  N9: U1.D14, LED1.3
  N10: U1.D13, LED1.2
  N11: U1.3V3, OLED1.4, ds1307.2
  N12: U1.D4, U3.1
  N13: U1.D19, btn.pin1
  N14: U1.D21, OLED1.1, ds1307.3
  N15: U1.D22, OLED1.2, ds1307.4
  N16: R1.Pin_1, M1.pin2, pwrsw.pin2
  N17: R2.Pin_0, U3.3
  N18: TP1.pin1, D2.C, R4.Pin_0, pwr.pin1
  N19: TP1.pin2, R5.Pin_1, pwr.pin2, solar.pin1
  N20: TP1.pin3, pwrsw.pin1
  N21: TP1.pin4, bat.pin2
  N22: TP1.pin5, bat.pin1
  N23: D2.A, solar.pin2
  N24: R3.Pin_0, LED1.1

custom parts:
  28BYJ-48 Driver Module: ULN2003 Driver Module for the 28BYJ-48 Unipolar Stepper Motor LED A - Blue wire - Bottom coil left LED B - Pink wire - Top coil left LED C - Yellow wire - Bottom coil right LED D - Orange wire - Top coil right Common rail - red Connector pins: blue - pink - yellow - orange - red Control pins - IN1 to IN4 Power pins - GND & Vmotor (5-12V) On/Off jumper (if removed, power to motor is cut).
  LuaNode32 / ESP32: ESP32 based LuaNode32
  TP4056: A DIP stand-in part for whatever IC you want. With 6 pins on a 300mil dual inline package (DIP) footprint.
  MT3608 Module: MT3608 Boost Converter Module Links: Aerosemi MT3608 2A Step Up Converter datasheet
  TL431 (sot23): 2% accuracy adjustable precision shunt regulator. sot-23-3
